# Fritzing sketch adhoc-network-nodeA+B (saved by Fritzing 0.9.2b)

parts:
  Raspberry_Pi1 = Raspberry Pi 2
  U1 = RF-LINK_TX [package=rf-link_tx]
  U2 = RF-LINK_RX [package=rf-link_rx]

nets:
  N1: Raspberry_Pi1.GPIO25, U1.DATA
  GND: Raspberry_Pi1.GND, U1.GND, U2.GND
  N2: Raspberry_Pi1.GPIO14, U2.DATA
  +5V: Raspberry_Pi1.5V, U1.+5V, U2.+5V
