# Fritzing sketch adhoc-network-nodeC (saved by Fritzing 0.9.2b)

parts:
  Raspberry_Pi1 = Raspberry Pi 2
  U2 = RF-LINK_RX [package=rf-link_rx]
  U3 = G3VM-61E1 [package=g3vm-61e1]

nets:
  GND: Raspberry_Pi1.GND, U2.GND, U3.P$3
  N1: Raspberry_Pi1.GPIO23, U3.P$2
  N2: Raspberry_Pi1.GPIO14, U2.DATA
  5V: Raspberry_Pi1.5V, U2.+5V, U3.P$1
