# Fritzing sketch adhoc-network-nodeD (saved by Fritzing 0.9.2b)

parts:
  Raspberry_Pi1 = Raspberry Pi 2
  U3 = G3VM-61E1 [package=g3vm-61e1]

nets:
  N1: Raspberry_Pi1.GND, U3.P$3
  N2: Raspberry_Pi1.GPIO23, U3.P$2
  N3: Raspberry_Pi1.5V, U3.P$1
