# Fritzing sketch attiny-wiring (saved by Fritzing 0.9.2b)

parts:
  U1 = RF-LINK_RX [package=rf-link_rx]
  U2 = RF-LINK_TX [package=rf-link_tx]
  U3 = attiny85 [package=dip]
  Raspberry_Pi1 = Raspberry Pi 2
  R1 = Resistor [tolerance=±5% resistance=220 package="0805 [SMD]"]
  R3 = Resistor [tolerance=±5% resistance=220 package="0805 [SMD]"]
  R4 = Resistor [tolerance=±5% resistance=220 package="0805 [SMD]"]
  R5 = Resistor [tolerance=±5% resistance=220 package="0805 [SMD]"]
  R2 = Resistor [tolerance=±5% resistance=220 package="0805 [SMD]"]

nets:
  N1: U1.DATA, U3.Pin_3
  +5V: U1.+5V, U2.+5V, U3.Pin_8, Raspberry_Pi1.5V
  N2: U2.DATA, Raspberry_Pi1.GPIO17
  GND: U2.GND, U3.Pin_4, Raspberry_Pi1.GND
  N3: U3.Pin_2, R1.Pin_0
  N4: U3.Pin_5, R5.Pin_0
  N5: U3.Pin_6, R4.Pin_0
  N6: U3.Pin_7, R3.Pin_0
  N7: Raspberry_Pi1.GPIO10, R5.Pin_1
  N8: Raspberry_Pi1.GPIO9, R4.Pin_1
  N9: Raspberry_Pi1.GPIO11, R3.Pin_1
  N10: Raspberry_Pi1.GPIO8, R2.Pin_1
  N11: Raspberry_Pi1.GPIO18, R1.Pin_1
