# Fritzing sketch usb-nano-wiring (saved by Fritzing 0.9.2b)

parts:
  Onderdeel2 = Arduino Nano (Rev3.0)
  U1 = RF-LINK_RX [package=rf-link_rx]
  U2 = RF-LINK_TX [package=rf-link_tx]

nets:
  N1: Onderdeel2.D2, Onderdeel2.D3, U1.DATA
  N2: Onderdeel2.D5, U2.DATA
  GND: Onderdeel2.GND, Onderdeel2.RESET, U1.GND, U2.GND
  +5V: Onderdeel2.5V, U1.+5V, U2.+5V
